# Fritzing sketch schema (saved by Fritzing 0.9.0b)
breadboards: 1

parts:
  Součástka1 = Spark Core (v1.0)
  J1 = Basic Servo
  V1 = DC Power [voltage=5]

nets:
  N1: Součástka1.A0, J1.pulse
  GND: Součástka1.GND, J1.gnd, V1.V-
  VIN: Součástka1.VIN, J1.vcc, V1.V+
